// Logisim project Life_with_joystick_only_end_columns.circ as structural Verilog
module main (
  input  Selecting
);

  wire _0_selecred, _1_selecred, _2_selecred, _3_selecred, _4_selecred, _5_selecred, _6_selecred,
       _7_selecred, _8_selecred, _9_selecred, _10_selecred, _11_selecred, _12_selecred, _13_selecred,
       _14_selecred, _15_selecred, _16_selecred, _17_selecred, _18_selecred, _19_selecred, _20_selecred,
       _21_selecred, _22_selecred, _23_selecred, _24_selecred, _25_selecred, _26_selecred, _27_selecred,
       _28_selecred, _29_selecred, _30_selecred, _31_selecred, button_needed, cdm_16_1_p1, cdm_16_1_p2,
       cdm_16_1_p4, cdm_16_1_p5, cdm_16_1_p6, cdm_16_1_p7, cdm_16_1_p8, change, Clock_cdm, Clock_life,
       Clock_select, column_needed, comparator_1_eq, comparator_2_eq, comparator_3_eq, comparator_4_eq,
       comparator_5_gt, half, mem, multiplexer_2_out, multiplexer_3_out, not_2_out, push_column, rd, word,
       x_glow, x_rise, y_glow, y_needed, y_rise;
  wire [4:0] buttons_shift_calculation_1_y_coordinate, x_shift;
  wire [15:0] _0_15, _16_31, addr, cdm_16_1_p13, cdm_16_1_p14, change_extended, controlled_buffer_1_out,
       data, default_data, first_changed, half_in, y_shift;
  wire [31:0] changed_column, Column_0, Column_1, Column_2, Column_3, Column_4, Column_5, Column_6, Column_7,
       Column_8, Column_9, Column_10, Column_11, Column_12, Column_13, Column_14, Column_15, Column_16,
       Column_17, Column_18, Column_19, Column_20, Column_21, Column_22, Column_23, Column_24, Column_25,
       Column_26, Column_27, Column_28, Column_29, Column_30, Column_31, multiplexer_7_out,
       n32x32_cells_1_condition_column_0, n32x32_cells_1_condition_column_1,
       n32x32_cells_1_condition_column_2, n32x32_cells_1_condition_column_3,
       n32x32_cells_1_condition_column_4, n32x32_cells_1_condition_column_5,
       n32x32_cells_1_condition_column_6, n32x32_cells_1_condition_column_7,
       n32x32_cells_1_condition_column_8, n32x32_cells_1_condition_column_9,
       n32x32_cells_1_condition_column_10, n32x32_cells_1_condition_column_11,
       n32x32_cells_1_condition_column_12, n32x32_cells_1_condition_column_13,
       n32x32_cells_1_condition_column_14, n32x32_cells_1_condition_column_15,
       n32x32_cells_1_condition_column_16, n32x32_cells_1_condition_column_17,
       n32x32_cells_1_condition_column_18, n32x32_cells_1_condition_column_19,
       n32x32_cells_1_condition_column_20, n32x32_cells_1_condition_column_21,
       n32x32_cells_1_condition_column_22, n32x32_cells_1_condition_column_23,
       n32x32_cells_1_condition_column_24, n32x32_cells_1_condition_column_25,
       n32x32_cells_1_condition_column_26, n32x32_cells_1_condition_column_27,
       n32x32_cells_1_condition_column_28, n32x32_cells_1_condition_column_29,
       n32x32_cells_1_condition_column_30, n32x32_cells_1_condition_column_31;

  Button button (.out(x_glow));
  Clock clock_1 (.out(Clock_cdm));
  Button button_2 (.out(y_rise));
  Button X (.out(change));
  Button button_3 (.out(y_glow));
  Clock #(.highDuration(19), .lowDuration(19)) clock_2 (.out(Clock_select));
  Button button_4 (.out(x_rise));
  Register #(.width(32)) register_1 (.D(changed_column), .en(_0_selecred), .Q(Column_0), .clk(Clock_cdm));  // open: clr
  Register #(.width(32)) register_2 (.D(changed_column), .en(_1_selecred), .Q(Column_1), .clk(Clock_cdm));  // open: clr
  Register #(.width(32)) register_3 (.D(changed_column), .en(_2_selecred), .Q(Column_2), .clk(Clock_cdm));  // open: clr
  Register #(.width(32)) register_4 (.D(changed_column), .en(_3_selecred), .Q(Column_3), .clk(Clock_cdm));  // open: clr
  Register #(.width(32)) register_5 (.D(changed_column), .en(_4_selecred), .Q(Column_4), .clk(Clock_cdm));  // open: clr
  Register #(.width(32)) register_6 (.D(changed_column), .en(_5_selecred), .Q(Column_5), .clk(Clock_cdm));  // open: clr
  Register #(.width(32)) register_7 (.D(changed_column), .en(_6_selecred), .Q(Column_6), .clk(Clock_cdm));  // open: clr
  Register #(.width(32)) register_8 (.D(changed_column), .en(_7_selecred), .Q(Column_7), .clk(Clock_cdm));  // open: clr
  Register #(.width(32)) register_9 (.D(changed_column), .en(_8_selecred), .Q(Column_8), .clk(Clock_cdm));  // open: clr
  Register #(.width(32)) register_10 (
    .D(changed_column), .en(_9_selecred), .Q(Column_9), .clk(Clock_cdm));  // open: clr
  Register #(.width(32)) register_11 (
    .D(changed_column), .en(_10_selecred), .Q(Column_10), .clk(Clock_cdm));  // open: clr
  Register #(.width(32)) register_12 (
    .D(changed_column), .en(_11_selecred), .Q(Column_11), .clk(Clock_cdm));  // open: clr
  Register #(.width(32)) register_13 (
    .D(changed_column), .en(_12_selecred), .Q(Column_12), .clk(Clock_cdm));  // open: clr
  Register #(.width(32)) register_14 (
    .D(changed_column), .en(_13_selecred), .Q(Column_13), .clk(Clock_cdm));  // open: clr
  Register #(.width(32)) register_15 (
    .D(changed_column), .en(_14_selecred), .Q(Column_14), .clk(Clock_cdm));  // open: clr
  Register #(.width(32)) register_16 (
    .D(changed_column), .en(_15_selecred), .Q(Column_15), .clk(Clock_cdm));  // open: clr
  Register #(.width(32)) register_17 (
    .D(changed_column), .en(_16_selecred), .Q(Column_16), .clk(Clock_cdm));  // open: clr
  Register #(.width(32)) register_18 (
    .D(changed_column), .en(_17_selecred), .Q(Column_17), .clk(Clock_cdm));  // open: clr
  Register #(.width(32)) register_19 (
    .D(changed_column), .en(_18_selecred), .Q(Column_18), .clk(Clock_cdm));  // open: clr
  Register #(.width(32)) register_20 (
    .D(changed_column), .en(_19_selecred), .Q(Column_19), .clk(Clock_cdm));  // open: clr
  Register #(.width(32)) register_21 (
    .D(changed_column), .en(_20_selecred), .Q(Column_20), .clk(Clock_cdm));  // open: clr
  Register #(.width(32)) register_22 (
    .D(changed_column), .en(_21_selecred), .Q(Column_21), .clk(Clock_cdm));  // open: clr
  Register #(.width(32)) register_23 (
    .D(changed_column), .en(_22_selecred), .Q(Column_22), .clk(Clock_cdm));  // open: clr
  Register #(.width(32)) register_24 (
    .D(changed_column), .en(_23_selecred), .Q(Column_23), .clk(Clock_cdm));  // open: clr
  Register #(.width(32)) register_25 (
    .D(changed_column), .en(_24_selecred), .Q(Column_24), .clk(Clock_cdm));  // open: clr
  Register #(.width(32)) register_26 (
    .D(changed_column), .en(_25_selecred), .Q(Column_25), .clk(Clock_cdm));  // open: clr
  Register #(.width(32)) register_27 (
    .D(changed_column), .en(_26_selecred), .Q(Column_26), .clk(Clock_cdm));  // open: clr
  Register #(.width(32)) register_28 (
    .D(changed_column), .en(_27_selecred), .Q(Column_27), .clk(Clock_cdm));  // open: clr
  Register #(.width(32)) register_29 (
    .D(changed_column), .en(_28_selecred), .Q(Column_28), .clk(Clock_cdm));  // open: clr
  Register #(.width(32)) register_30 (
    .D(changed_column), .en(_29_selecred), .Q(Column_29), .clk(Clock_cdm));  // open: clr
  Register #(.width(32)) register_31 (
    .D(changed_column), .en(_30_selecred), .Q(Column_30), .clk(Clock_cdm));  // open: clr
  Register #(.width(32)) register_32 (
    .D(changed_column), .en(_31_selecred), .Q(Column_31), .clk(Clock_cdm));  // open: clr
  Clock #(.highDuration(5), .lowDuration(5)) clock_3 (.out(Clock_life));
  buttons_shift_calculation buttons_shift_calculation_1 (
    .x_coordinate(x_shift), .y_coordinate(buttons_shift_calculation_1_y_coordinate), .x_rise(x_rise),
    .x_glow(x_glow), .y_rise(y_rise), .y_glow(y_glow));
  assign change_extended = {{15{1'b0}}, change};  // Bit_Extender bit_extender_1
  Comparator #(.width(16), .mode("unsigned")) comparator_1 (
    .a(addr), .b(16'hcafe), .eq(comparator_1_eq));  // open: gt, lt
  Comparator #(.width(16), .mode("unsigned")) comparator_2 (
    .a(addr), .b(16'hbeef), .eq(comparator_2_eq));  // open: gt, lt
  Comparator #(.width(16), .mode("unsigned")) comparator_3 (
    .a(addr), .b(16'hbabe), .eq(comparator_3_eq));  // open: gt, lt
  Comparator #(.width(16)) comparator_4 (.a(addr), .b(16'hbabe), .eq(comparator_4_eq));  // open: gt, lt
  Multiplexer #(.select(5), .width(32), .enable("false")) multiplexer_1 (
    .in0(Column_0), .in1(Column_1), .in2(Column_2), .in3(Column_3), .in4(Column_4), .in5(Column_5),
    .in6(Column_6), .in7(Column_7), .in8(Column_8), .in9(Column_9), .in10(Column_10), .in11(Column_11),
    .in12(Column_12), .in13(Column_13), .in14(Column_14), .in15(Column_15), .in16(Column_16),
    .in17(Column_17), .in18(Column_18), .in19(Column_19), .in20(Column_20), .in21(Column_21),
    .in22(Column_22), .in23(Column_23), .in24(Column_24), .in25(Column_25), .in26(Column_26),
    .in27(Column_27), .in28(Column_28), .in29(Column_29), .in30(Column_30), .in31(Column_31),
    .out({_16_31, _0_15}), .sel(x_shift));
  // Probe on x_shift
  // Probe on buttons_shift_calculation_1_y_coordinate
  and and_1 (button_needed, rd, mem, change, comparator_1_eq);
  and and_2 (y_needed, rd, mem, change, comparator_2_eq);
  and and_3 (column_needed, rd, mem, change, comparator_3_eq);
  and and_4 (push_column, ~rd, mem, word, comparator_4_eq);  // AND_Gate
  not not_1 (half, comparator_5_gt);
  Comparator #(.width(16), .mode("unsigned")) comparator_5 (
    .a(y_shift), .b(16'hf), .gt(comparator_5_gt));  // open: eq, lt
  assign y_shift = {{11{1'b0}}, buttons_shift_calculation_1_y_coordinate};  // Bit_Extender bit_extender_2
  Demultiplexer #(.select(5), .enable("false")) demultiplexer_1 (
    .out0(_0_selecred), .out1(_1_selecred), .out2(_2_selecred), .out3(_3_selecred), .out4(_4_selecred),
    .out5(_5_selecred), .out6(_6_selecred), .out7(_7_selecred), .out8(_8_selecred), .out9(_9_selecred),
    .out10(_10_selecred), .out11(_11_selecred), .out12(_12_selecred), .out13(_13_selecred),
    .out14(_14_selecred), .out15(_15_selecred), .out16(_16_selecred), .out17(_17_selecred),
    .out18(_18_selecred), .out19(_19_selecred), .out20(_20_selecred), .out21(_21_selecred),
    .out22(_22_selecred), .out23(_23_selecred), .out24(_24_selecred), .out25(_25_selecred),
    .out26(_26_selecred), .out27(_27_selecred), .out28(_28_selecred), .out29(_29_selecred),
    .out30(_30_selecred), .out31(_31_selecred), .in(1'b1), .sel(x_shift));
  DotMatrix #(.matrixcols(32), .matrixrows(32)) dotmatrix_1 (
    .col0(n32x32_cells_1_condition_column_0), .col1(n32x32_cells_1_condition_column_1),
    .col2(n32x32_cells_1_condition_column_2), .col3(n32x32_cells_1_condition_column_3),
    .col4(n32x32_cells_1_condition_column_4), .col5(n32x32_cells_1_condition_column_5),
    .col6(n32x32_cells_1_condition_column_6), .col7(n32x32_cells_1_condition_column_7),
    .col8(n32x32_cells_1_condition_column_8), .col9(n32x32_cells_1_condition_column_9),
    .col10(n32x32_cells_1_condition_column_10), .col11(n32x32_cells_1_condition_column_11),
    .col12(n32x32_cells_1_condition_column_12), .col13(n32x32_cells_1_condition_column_13),
    .col14(n32x32_cells_1_condition_column_14), .col15(n32x32_cells_1_condition_column_15),
    .col16(n32x32_cells_1_condition_column_16), .col17(n32x32_cells_1_condition_column_17),
    .col18(n32x32_cells_1_condition_column_18), .col19(n32x32_cells_1_condition_column_19),
    .col20(n32x32_cells_1_condition_column_20), .col21(n32x32_cells_1_condition_column_21),
    .col22(n32x32_cells_1_condition_column_22), .col23(n32x32_cells_1_condition_column_23),
    .col24(n32x32_cells_1_condition_column_24), .col25(n32x32_cells_1_condition_column_25),
    .col26(n32x32_cells_1_condition_column_26), .col27(n32x32_cells_1_condition_column_27),
    .col28(n32x32_cells_1_condition_column_28), .col29(n32x32_cells_1_condition_column_29),
    .col30(n32x32_cells_1_condition_column_30), .col31(n32x32_cells_1_condition_column_31));
  _32x32_cells u_32x32_cells_1 (
    .Selecting(Selecting), .Clock(multiplexer_2_out), .Column_0(Column_0), .Column_1(Column_1),
    .Column_2(Column_2), .Column_3(Column_3), .Column_4(Column_4), .Column_5(Column_5), .Column_6(Column_6),
    .Column_7(Column_7), .Column_8(Column_8), .Column_9(Column_9), .Column_10(Column_10),
    .Column_11(Column_11), .Column_12(Column_12), .Column_13(Column_13), .Column_14(Column_14),
    .Column_15(Column_15), .Column_16(Column_16), .Column_17(Column_17), .Column_18(Column_18),
    .Column_19(Column_19), .Column_20(Column_20), .Column_21(Column_21), .Column_22(Column_22),
    .Column_23(Column_23), .Column_24(Column_24), .Column_25(Column_25), .Column_26(Column_26),
    .Column_27(Column_27), .Column_28(Column_28), .Column_29(Column_29), .Column_30(Column_30),
    .Column_31(Column_31), .condition_column_0(n32x32_cells_1_condition_column_0),
    .condition_column_1(n32x32_cells_1_condition_column_1),
    .condition_column_2(n32x32_cells_1_condition_column_2),
    .condition_column_3(n32x32_cells_1_condition_column_3),
    .condition_column_6(n32x32_cells_1_condition_column_6),
    .condition_column_5(n32x32_cells_1_condition_column_5),
    .condition_column_7(n32x32_cells_1_condition_column_7),
    .condition_column_4(n32x32_cells_1_condition_column_4),
    .condition_column_10(n32x32_cells_1_condition_column_10),
    .condition_column_9(n32x32_cells_1_condition_column_9),
    .condition_column_11(n32x32_cells_1_condition_column_11),
    .condition_column_8(n32x32_cells_1_condition_column_8),
    .condition_column_14(n32x32_cells_1_condition_column_14),
    .condition_column_13(n32x32_cells_1_condition_column_13),
    .condition_column_15(n32x32_cells_1_condition_column_15),
    .condition_column_12(n32x32_cells_1_condition_column_12),
    .condition_column_18(n32x32_cells_1_condition_column_18),
    .condition_column_17(n32x32_cells_1_condition_column_17),
    .condition_column_19(n32x32_cells_1_condition_column_19),
    .condition_column_16(n32x32_cells_1_condition_column_16),
    .condition_column_22(n32x32_cells_1_condition_column_22),
    .condition_column_23(n32x32_cells_1_condition_column_23),
    .condition_column_20(n32x32_cells_1_condition_column_20),
    .condition_column_21(n32x32_cells_1_condition_column_21),
    .condition_column_26(n32x32_cells_1_condition_column_26),
    .condition_column_25(n32x32_cells_1_condition_column_25),
    .condition_column_27(n32x32_cells_1_condition_column_27),
    .condition_column_24(n32x32_cells_1_condition_column_24),
    .condition_column_30(n32x32_cells_1_condition_column_30),
    .condition_column_29(n32x32_cells_1_condition_column_29),
    .condition_column_31(n32x32_cells_1_condition_column_31),
    .condition_column_28(n32x32_cells_1_condition_column_28));
  // Probe on cdm_16_1_p1
  // RAM ram_1: pin names not known; wires that end beside it: addr, word, mem, Clock_cdm, rd, data
  Multiplexer #(.enable("false")) multiplexer_2 (
    .in0(Clock_life), .in1(multiplexer_3_out), .out(multiplexer_2_out), .sel(Selecting));
  // Probe on cdm_16_1_p4
  // Probe on cdm_16_1_p2
  // CdM_16 cdm_16_1: pin names not known; wires that end beside it: cdm_16_1_p1, cdm_16_1_p2, Clock_cdm, cdm_16_1_p4, cdm_16_1_p5, cdm_16_1_p6, cdm_16_1_p7, cdm_16_1_p8, mem, rd, word, addr, cdm_16_1_p13, cdm_16_1_p14
  Multiplexer #(.enable("false")) multiplexer_3 (
    .in0(change), .in1(Clock_select), .out(multiplexer_3_out), .sel(change));
  // Probe on cdm_16_1_p5
  // Probe on cdm_16_1_p7
  // Probe on cdm_16_1_p6
  // Probe on cdm_16_1_p8
  Multiplexer #(.select(3), .width(16), .enable("false")) multiplexer_4 (
    .in0(default_data), .in1(y_shift), .in2(half_in), .in4(change_extended), .out(cdm_16_1_p14),
    .sel({button_needed, column_needed, y_needed}));  // open: in3, in5, in6, in7
  assign controlled_buffer_1_out = push_column ? cdm_16_1_p13 : 16'bz;  // Controlled_Buffer controlled_buffer_1
  Multiplexer #(.width(16), .enable("false")) multiplexer_5 (.in0(_16_31), .in1(_0_15), .out(half_in), .sel(half));
  Multiplexer #(.width(16), .enable("false")) multiplexer_6 (
    .in0(half_in), .in1(controlled_buffer_1_out), .out(first_changed), .sel(not_2_out));
  assign default_data = rd ? data : 16'bz;  // Controlled_Buffer controlled_buffer_2
  not not_2 (not_2_out, rd);
  assign data = not_2_out ? cdm_16_1_p13 : 16'bz;  // Controlled_Buffer controlled_buffer_3
  Multiplexer #(.width(32), .enable("false")) multiplexer_7 (
    .in0({first_changed, _0_15}), .in1({_16_31, first_changed}), .out(multiplexer_7_out), .sel(half));
  Multiplexer #(.width(32), .enable("false")) multiplexer_8 (
    .in0({_16_31, _0_15}), .in1(multiplexer_7_out), .out(changed_column), .sel(change));

  // Other names for the same wires on the sheet: column_out[31:0] = {_16_31, _0_15}; first_changed[31:16] = _16_31;
  //   second_changed[31:0] = {first_changed, _0_15}; output[15:0] = first_changed
endmodule

module \cell  (
  input  Selected,
  input  Selecting,
  input  Clock,
  input  Left_up_in,
  input  Middle_up_in,
  input  Right_up_in,
  input  Left_middle_in,
  input  Right_middle_in,
  input  Left_down_in,
  input  Middle_down_in,
  input  Right_down_in,
  output Left_up_out,
  output Middle_up_out,
  output Right_up_out,
  output Left_middle_out,
  output Right_middle_out,
  output Left_down_out,
  output Middle_down_out,
  output Right_down_out
);

  wire multiplexer_1_out, Next;
  wire [7:0] Sum;

  Multiplexer #(.enable("false")) multiplexer_1 (.in0(Next), .in1(Selected), .out(multiplexer_1_out), .sel(Selecting));
  Register #(.width(1)) Current (.D(multiplexer_1_out), .Q(Left_down_out), .clk(Clock));  // open: en, clr
  next_phase_selector next_phase_selector_1 (.Current(Left_down_out), .Sum(Sum), .next_state(Next));
  sum_of_neighbours sum_of_neighbours_1 (
    .in_1(Left_up_in), .in_2(Middle_up_in), .in_3(Right_up_in), .in_4(Left_middle_in),
    .in_5(Right_middle_in), .in_6(Right_down_in), .in_7(Middle_down_in), .in_8(Left_down_in), .Sum(Sum));

  assign Left_middle_out = Left_down_out;
  assign Left_up_out = Left_down_out;
  assign Middle_down_out = Left_down_out;
  assign Middle_up_out = Left_down_out;
  assign Right_down_out = Left_down_out;
  assign Right_middle_out = Left_down_out;
  assign Right_up_out = Left_down_out;

  // Other names for the same wires on the sheet: Current = Left_down_out; Left_down = Left_down_in;
  //   Left_middle = Left_middle_in; Left_up = Left_up_in; Middle_down = Middle_down_in; Middle_up = Middle_up_in;
  //   Right_down = Right_down_in; Right_middle = Right_middle_in; Right_up = Right_up_in
endmodule

module sum_of_neighbours (
  input  in_1,
  input  in_2,
  input  in_3,
  input  in_4,
  input  in_5,
  input  in_6,
  input  in_7,
  input  in_8,
  output [7:0] Sum
);

  BitAdder #(.width(1)) bitadder_1 (
    .in0(in_1), .in1(in_2), .in2(in_3), .in3(in_4), .in4(in_5), .in5(in_6), .in6(in_7), .in7(in_8),
    .out(Sum[3:0]));

  assign Sum[7:4] = 4'b0000;
endmodule

module next_phase_selector (
  input  Current,
  input  [7:0] Sum,
  output next_state
);

  wire comparator_1_eq, for_alive, for_dead;

  Comparator comparator_1 (.a(Sum), .b(8'h2), .eq(comparator_1_eq));  // open: gt, lt
  Comparator comparator_2 (.a(Sum), .b(8'h3), .eq(for_dead));  // open: gt, lt
  or or_1 (for_alive, comparator_1_eq, for_dead);
  Multiplexer #(.enable("false")) multiplexer_1 (.in0(for_dead), .in1(for_alive), .out(next_state), .sel(Current));
endmodule
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