// Logisim project myBlas.circ as structural Verilog: 4 circuits, main circuit NEG
module NEG (
  input  [7:0] in_1,
  output [7:0] out_2
);

  // NOT_Gate not_1 has open pins: in=in_1, out=open
  // NSU_2023_T05L1e10_inc inc_1: pin names not known; wires that end beside it: out_2
endmodule

module inc (
  input  [7:0] X,
  output [7:0] R,
  output Cout
);

  wire [7:1] and_1_out;

  assign {Cout, and_1_out} = {and_1_out, 1'b1} & X;  // AND_Gate and_1, 8 bits wide
  assign R = X ^ {and_1_out, 1'b1};  // XOR_Gate xor_1, 8 bits wide
endmodule

module add (
  input  [7:0] A,
  input  [7:0] B,
  input  Cin,
  output [7:0] sum,
  output Cout
);

  wire [6:0] or_1_out;
  wire [7:0] and_1_out, and_2_out, and_3_out;

  assign and_1_out = A & B;  // AND_Gate and_1, 8 bits wide
  assign and_2_out = B & {or_1_out, Cin};  // AND_Gate and_2, 8 bits wide
  assign and_3_out = A & {or_1_out, Cin};  // AND_Gate and_3, 8 bits wide
  assign {Cout, or_1_out} = and_1_out | and_2_out | and_3_out;  // OR_Gate or_1, 8 bits wide
  assign sum = A ^ {or_1_out, Cin} ^ B;  // XOR_Gate xor_1, 8 bits wide
endmodule

module sub (
  input  [7:0] in_1,
  input  in_2,
  input  [7:0] in_3,
  output [7:0] out_4,
  output out_5
);

  wire [7:0] inc_1_r, neg_1_out_2;

  NEG neg_1 (.in_1(in_3), .out_2(neg_1_out_2));
  inc inc_1 (.X(neg_1_out_2), .R(inc_1_r));  // open: Cout
  add add_1 (.A(in_1), .B(inc_1_r), .Cin(in_2), .sum(out_4), .Cout(out_5));
endmodule
