// Logisim project buttons_input_two_columns_testing.circ as structural Verilog: 1 circuit, main circuit main
module main (
);

  wire _0_selecred, _1_selecred, _2_selecred, _3_selecred, _4_selecred, _5_selecred, _6_selecred,
       _7_selecred, _8_selecred, _9_selecred, _10_selecred, _11_selecred, _12_selecred, _13_selecred,
       _14_selecred, _15_selecred, _16_selecred, _17_selecred, _18_selecred, _19_selecred, _20_selecred,
       _21_selecred, _22_selecred, _23_selecred, _24_selecred, _25_selecred, _26_selecred, _27_selecred,
       _28_selecred, _29_selecred, _30_selecred, _31_selecred, and_4_out, button_needed, cdm_16_1_p1,
       cdm_16_1_p2, cdm_16_1_p4, cdm_16_1_p5, cdm_16_1_p6, cdm_16_1_p7, cdm_16_1_p8, change, Clock,
       column_needed, comparator_1_eq, comparator_2_eq, comparator_3_eq, comparator_4_eq, comparator_5_gt,
       half, mem, not_1_out, rd, word, x_glow, x_rise, y_glow, y_needed, y_rise;
  wire [4:0] buttons_shift_calculation_1_y_coordinate, x_shift;
  wire [15:0] _0_15, _16_31, addr, cdm_16_1_p13, cdm_16_1_p14, change_extended, controlled_buffer_1_out,
       data, default_data, first_changed, half_in, y_shift;
  wire [31:0] changed_column, multiplexer_4_out, register_1_q, register_2_q, undriven, undriven_2,
       undriven_3, undriven_4, undriven_5, undriven_6, undriven_7, undriven_8, undriven_9, undriven_10,
       undriven_11, undriven_12, undriven_13, undriven_14, undriven_15, undriven_16, undriven_17,
       undriven_18, undriven_19, undriven_20, undriven_21, undriven_22, undriven_23, undriven_24,
       undriven_25, undriven_26, undriven_27, undriven_28, undriven_29, undriven_30;

  Button button_1 (.out(x_glow));
  assign change_extended = {{15{1'b0}}, change};  // Bit_Extender bit_extender_1
  Button button_2 (.out(y_rise));
  Button button_3 (.out(change));
  Button button_4 (.out(y_glow));
  Clock clock_1 (.out(Clock));
  // Debugger debugger_1: pin names not known
  buttons_shift_calculation buttons_shift_calculation_1 (
    .x_coordinate(x_shift), .y_coordinate(buttons_shift_calculation_1_y_coordinate), .x_rise(x_rise),
    .x_glow(x_glow), .y_rise(y_rise), .y_glow(y_glow));
  Button button_5 (.out(x_rise));
  // RAM ram_1: pin names not known; wires that end beside it: addr, word, mem, Clock, rd, data
  // Probe on cdm_16_1_p1
  // Probe on cdm_16_1_p2
  // Probe on x_shift
  // Probe on buttons_shift_calculation_1_y_coordinate
  // Probe on cdm_16_1_p5
  // Probe on cdm_16_1_p4
  // CdM_16 cdm_16_1: pin names not known; wires that end beside it: cdm_16_1_p1, cdm_16_1_p2, Clock, cdm_16_1_p4, cdm_16_1_p5, cdm_16_1_p6, cdm_16_1_p7, cdm_16_1_p8, mem, rd, word, addr, cdm_16_1_p13, cdm_16_1_p14
  assign y_shift = {{11{1'b0}}, buttons_shift_calculation_1_y_coordinate};  // Bit_Extender bit_extender_2
  // Probe on cdm_16_1_p6
  // Probe on cdm_16_1_p8
  // Probe on cdm_16_1_p7
  Multiplexer #(.select(3), .width(16), .enable("false")) multiplexer_1 (
    .in0(default_data), .in1(y_shift), .in2(half_in), .in4(change_extended), .out(cdm_16_1_p14),
    .sel({button_needed, column_needed, y_needed}));  // open: in3, in5, in6, in7
  Comparator #(.width(16), .mode("unsigned")) comparator_1 (
    .a(addr), .b(16'hcafe), .eq(comparator_1_eq));  // open: gt, lt
  Comparator #(.width(16), .mode("unsigned")) comparator_2 (
    .a(addr), .b(16'hbeef), .eq(comparator_2_eq));  // open: gt, lt
  Comparator #(.width(16), .mode("unsigned")) comparator_3 (
    .a(addr), .b(16'hbabe), .eq(comparator_3_eq));  // open: gt, lt
  Comparator #(.width(16)) comparator_4 (.a(addr), .b(16'hbabe), .eq(comparator_4_eq));  // open: gt, lt
  and and_1 (button_needed, rd, mem, change, comparator_1_eq);
  and and_2 (y_needed, rd, mem, change, comparator_2_eq);
  and and_3 (column_needed, rd, mem, change, comparator_3_eq);
  and and_4 (and_4_out, ~rd, mem, word, comparator_4_eq);  // AND_Gate
  Demultiplexer #(.select(5), .enable("false")) demultiplexer_1 (
    .out0(_0_selecred), .out1(_1_selecred), .out2(_2_selecred), .out3(_3_selecred), .out4(_4_selecred),
    .out5(_5_selecred), .out6(_6_selecred), .out7(_7_selecred), .out8(_8_selecred), .out9(_9_selecred),
    .out10(_10_selecred), .out11(_11_selecred), .out12(_12_selecred), .out13(_13_selecred),
    .out14(_14_selecred), .out15(_15_selecred), .out16(_16_selecred), .out17(_17_selecred),
    .out18(_18_selecred), .out19(_19_selecred), .out20(_20_selecred), .out21(_21_selecred),
    .out22(_22_selecred), .out23(_23_selecred), .out24(_24_selecred), .out25(_25_selecred),
    .out26(_26_selecred), .out27(_27_selecred), .out28(_28_selecred), .out29(_29_selecred),
    .out30(_30_selecred), .out31(_31_selecred), .in(1'b1), .sel(x_shift));
  assign controlled_buffer_1_out = and_4_out ? cdm_16_1_p13 : 16'bz;  // Controlled_Buffer controlled_buffer_1
  Multiplexer #(.width(16), .enable("false")) multiplexer_2 (.in0(_16_31), .in1(_0_15), .out(half_in), .sel(half));
  Comparator #(.width(16), .mode("unsigned")) comparator_5 (
    .a(y_shift), .b(16'hf), .gt(comparator_5_gt));  // open: eq, lt
  Multiplexer #(.width(16), .enable("false")) multiplexer_3 (
    .in0(half_in), .in1(controlled_buffer_1_out), .out(first_changed), .sel(not_1_out));
  not not_1 (not_1_out, rd);
  assign data = not_1_out ? cdm_16_1_p13 : 16'bz;  // Controlled_Buffer controlled_buffer_2
  assign default_data = rd ? data : 16'bz;  // Controlled_Buffer controlled_buffer_3
  not not_2 (half, comparator_5_gt);
  Multiplexer #(.width(32), .enable("false")) multiplexer_4 (
    .in0({first_changed, _0_15}), .in1({_16_31, first_changed}), .out(multiplexer_4_out), .sel(half));
  Multiplexer #(.width(32), .enable("false")) multiplexer_5 (
    .in0({_16_31, _0_15}), .in1(multiplexer_4_out), .out(changed_column), .sel(change));
  Register #(.width(32)) register_1 (.D(changed_column), .en(_0_selecred), .Q(register_1_q), .clk(Clock));  // open: clr
  Register #(.width(32)) register_2 (.D(changed_column), .en(_1_selecred), .Q(register_2_q), .clk(Clock));  // open: clr
  DotMatrix #(.matrixcols(32), .matrixrows(32)) dotmatrix_1 (
    .col0(register_1_q), .col1(register_2_q), .col2(undriven), .col3(undriven_2), .col4(undriven_3),
    .col5(undriven_4), .col6(undriven_5), .col7(undriven_6), .col8(undriven_7), .col9(undriven_8),
    .col10(undriven_9), .col11(undriven_10), .col12(undriven_11), .col13(undriven_12), .col14(undriven_13),
    .col15(undriven_14), .col16(undriven_15), .col17(undriven_16), .col18(undriven_17), .col19(undriven_18),
    .col20(undriven_19), .col21(undriven_20), .col22(undriven_21), .col23(undriven_22), .col24(undriven_23),
    .col25(undriven_24), .col26(undriven_25), .col27(undriven_26), .col28(undriven_27), .col29(undriven_28),
    .col30(undriven_29), .col31(undriven_30));
  Multiplexer #(.select(5), .width(32), .enable("false")) multiplexer_6 (
    .in0(register_1_q), .in1(register_2_q), .in2(undriven), .in3(undriven_2), .in4(undriven_3),
    .in5(undriven_4), .in6(undriven_5), .in7(undriven_6), .in8(undriven_7), .in9(undriven_8),
    .in10(undriven_9), .in11(undriven_10), .in12(undriven_11), .in13(undriven_12), .in14(undriven_13),
    .in15(undriven_14), .in16(undriven_15), .in17(undriven_16), .in18(undriven_17), .in19(undriven_18),
    .in20(undriven_19), .in21(undriven_20), .in22(undriven_21), .in23(undriven_22), .in24(undriven_23),
    .in25(undriven_24), .in26(undriven_25), .in27(undriven_26), .in28(undriven_27), .in29(undriven_28),
    .in30(undriven_29), .in31(undriven_30), .out({_16_31, _0_15}), .sel(x_shift));

  // Other names for the same wires on the sheet: column_out[31:0] = {_16_31, _0_15};
  //   second_changed[31:0] = {first_changed, _0_15}; first_changed[31:16] = _16_31; output[15:0] = first_changed
endmodule
