// Logisim project buttons_shift_calculation_local.circ as structural Verilog: 1 circuit, main circuit joystick_shift_calculation
module joystick_shift_calculation (
  output [4:0] x_coordinate,
  output [4:0] y_coordinate
);

  wire Clock, x_glow, x_glow_allowed, x_rise, x_rise_allowed, y_glow, y_glow_allowed, y_rise, y_rise_allowed;
  wire [1:0] and_1_out, and_2_out;
  wire [4:0] multiplexer_1_out, multiplexer_2_out, multiplexer_3_out, multiplexer_4_out, multiplexer_5_out,
       multiplexer_6_out, x_add_res, x_sub_res, y_add_res, y_sub_res;

  or or_1 (Clock, x_rise, x_glow, y_rise, y_glow);
  Button button_1 (.out(x_rise));
  Button button_2 (.out(x_glow));
  Button button_3 (.out(y_rise));
  Button button_4 (.out(y_glow));
  Comparator #(.width(5)) comparator_1 (.a(x_coordinate), .b({5{1'b0}}), .gt(x_glow_allowed));  // open: eq, lt
  Comparator #(.width(5)) comparator_2 (.a(x_coordinate), .b(5'b01111), .lt(x_rise_allowed));  // open: gt, eq
  Comparator #(.width(5)) comparator_3 (.a(y_coordinate), .b({5{1'b0}}), .gt(y_glow_allowed));  // open: eq, lt
  Comparator #(.width(5)) comparator_4 (.a(y_coordinate), .b(5'b01111), .lt(y_rise_allowed));  // open: gt, eq
  Subtractor #(.width(5)) subtractor_1 (.a(x_coordinate), .b(5'b00001), .out(x_sub_res));  // open: bin, bout
  Adder #(.width(5)) adder_1 (.a(x_coordinate), .b(5'b00001), .out(x_add_res));  // open: cin, cout
  Subtractor #(.width(5)) subtractor_2 (.a(y_coordinate), .b(5'b00001), .out(y_sub_res));  // open: bin, bout
  Adder #(.width(5)) adder_2 (.a(y_coordinate), .b(5'b00001), .out(y_add_res));  // open: cin, cout
  Multiplexer #(.width(5), .enable("false")) multiplexer_1 (
    .in0(x_coordinate), .in1(x_sub_res), .out(multiplexer_1_out), .sel(x_glow));
  Multiplexer #(.width(5), .enable("false")) multiplexer_2 (
    .in0(x_coordinate), .in1(x_add_res), .out(multiplexer_2_out), .sel(x_rise));
  Multiplexer #(.width(5), .enable("false")) multiplexer_3 (
    .in0(y_coordinate), .in1(y_sub_res), .out(multiplexer_3_out), .sel(y_glow));
  Multiplexer #(.width(5), .enable("false")) multiplexer_4 (
    .in0(y_coordinate), .in1(y_add_res), .out(multiplexer_4_out), .sel(y_rise));
  and and_1 (and_1_out[0], x_glow_allowed, x_glow);
  and and_2 (and_2_out[0], y_glow_allowed, y_glow);
  Multiplexer #(.select(2), .width(5), .enable("false")) multiplexer_5 (
    .in0(x_coordinate), .in1(multiplexer_1_out), .in2(multiplexer_2_out), .in3(x_coordinate),
    .out(multiplexer_5_out), .sel(and_1_out));
  Multiplexer #(.select(2), .width(5), .enable("false")) multiplexer_6 (
    .in0(y_coordinate), .in1(multiplexer_3_out), .in2(multiplexer_4_out), .in3(y_coordinate),
    .out(multiplexer_6_out), .sel(and_2_out));
  Register #(.width(5), .trigger("falling")) u_x_coordinate (
    .D(multiplexer_5_out), .Q(x_coordinate), .clk(Clock));  // open: en, clr
  // Probe on x_coordinate
  and and_3 (and_1_out[1], x_rise_allowed, x_rise);
  Register #(.width(5), .trigger("falling")) u_y_coordinate (
    .D(multiplexer_6_out), .Q(y_coordinate), .clk(Clock));  // open: en, clr
  // Probe on y_coordinate
  and and_4 (and_2_out[1], y_rise_allowed, y_rise);
endmodule
