// Logisim project keyboard_input_and_output.circ as structural Verilog: 1 circuit, main circuit main
module main (
);

  wire and_1_out, cdm_16_1_p1, cdm_16_1_p2, cdm_16_1_p4, cdm_16_1_p5, cdm_16_1_p6, cdm_16_1_p7, cdm_16_1_p8,
       Clock, comparator_1_eq, comparator_2_eq, mem, memMux, not_1_out, rd, word;
  wire [6:0] keyboard_1_data;
  wire [15:0] addr, cdm_16_1_p13, cdm_16_1_p14, controlled_buffer_2_out, data, kbdMemIn;

  Clock clock_1 (.out(Clock));
  // Debugger debugger_1: pin names not known
  // RAM ram_1: pin names not known; wires that end beside it: addr, word, mem, Clock, rd, data
  // Probe on cdm_16_1_p2
  // Probe on cdm_16_1_p1
  // Probe on cdm_16_1_p4
  // Probe on cdm_16_1_p5
  // CdM_16 cdm_16_1: pin names not known; wires that end beside it: cdm_16_1_p1, cdm_16_1_p2, Clock, cdm_16_1_p4, cdm_16_1_p5, cdm_16_1_p6, cdm_16_1_p7, cdm_16_1_p8, mem, rd, word, addr, cdm_16_1_p13, cdm_16_1_p14
  // Probe on cdm_16_1_p6
  // Probe on cdm_16_1_p7
  // Probe on cdm_16_1_p8
  Comparator #(.width(16)) comparator_1 (.a(addr), .b(16'hbeef), .eq(comparator_1_eq));  // open: gt, lt
  Multiplexer #(.width(16), .enable("false")) multiplexer_1 (
    .in0(controlled_buffer_2_out), .in1(kbdMemIn), .out(cdm_16_1_p14), .sel(memMux));
  Comparator #(.width(16)) comparator_2 (.a(addr), .b(16'hdead), .eq(comparator_2_eq));  // open: gt, lt
  and and_1 (and_1_out, ~rd, mem, ~word, comparator_2_eq);  // AND_Gate
  and and_2 (memMux, rd, mem, ~word, comparator_1_eq);  // AND_Gate
  TTY tty_1 (.data(cdm_16_1_p13[6:0]), .clk(and_1_out));  // open: we, clr
  Keyboard #(.trigger("falling")) keyboard_1 (.clk(memMux), .data(keyboard_1_data));  // open: re, clr, avail
  not not_1 (not_1_out, rd);
  assign data = not_1_out ? cdm_16_1_p13 : 16'bz;  // Controlled_Buffer controlled_buffer_1
  assign controlled_buffer_2_out = rd ? data : 16'bz;  // Controlled_Buffer controlled_buffer_2
  assign kbdMemIn = {{9{1'b0}}, keyboard_1_data};  // Bit_Extender bit_extender_1
endmodule
