// Logisim project simplest_scheme.circ as structural Verilog: 1 circuit, main circuit main
module main (
);

  wire cdm_16_1_p1, cdm_16_1_p2, cdm_16_1_p3, cdm_16_1_p4, mem, not_1_out, ram_1_p4, rd, word;
  wire [15:0] addr, cdm_16_1_p9, cdm_16_1_p10, data;

  // Probe on cdm_16_1_p1
  // Probe on cdm_16_1_p3
  // CdM_16 cdm_16_1: pin names not known; wires that end beside it: cdm_16_1_p1, cdm_16_1_p2, cdm_16_1_p3, cdm_16_1_p4, mem, rd, word, addr, cdm_16_1_p9, cdm_16_1_p10
  Clock clock_1 (.out(cdm_16_1_p2));
  // Debugger debugger_1: pin names not known
  // Probe on cdm_16_1_p4
  not not_1 (not_1_out, rd);
  assign data = not_1_out ? cdm_16_1_p9 : 16'bz;  // Controlled_Buffer controlled_buffer_1
  assign cdm_16_1_p10 = rd ? data : 16'bz;  // Controlled_Buffer controlled_buffer_2
  // RAM ram_1: pin names not known; wires that end beside it: addr, word, mem, ram_1_p4, rd, data
  Clock clock_2 (.out(ram_1_p4));
endmodule
